# Fritzing sketch Audioberry Sketch v4 (saved by Fritzing 0.9.4)
circuit board: 10cm x 6cm
breadboards: 1

parts:
  Bu_ST_1 = Pushbutton [package="[THT]"]
  Rotary_Encoder = mystery part, 5 pins [chip_label="Rotary Encoder"]
  OLED = Grove OLED 128x96
  NEOPIXEL1 = Neopixel Strip -- White (30/m) [part_number=1376]
  Raspberry_Pi = Raspberry Pi 3 [part_number=RPI-3-V1.2]
  Bn_ST_2 = Pushbutton [package="[THT]"]

nets:
  N1: Bu_ST_1.Pin_1, Bu_ST_1.Pin_2, Raspberry_Pi.GPIO12
  GND: Bu_ST_1.Pin_3, Bu_ST_1.Pin_4, Rotary_Encoder.pin5, OLED.GND, NEOPIXEL1.GND, Raspberry_Pi.GND, Bn_ST_2.Pin_3, Bn_ST_2.Pin_4
  N2: Rotary_Encoder.pin1, Raspberry_Pi.GPIO13
  N3: Rotary_Encoder.pin2, Raspberry_Pi.GPIO6
  N4: Rotary_Encoder.pin3, Raspberry_Pi.GPIO5
  VCC: Rotary_Encoder.pin4, OLED.VCC, NEOPIXEL1.+5V, Raspberry_Pi.5V
  N5: OLED.SDA, Raspberry_Pi.GPIO2
  N6: OLED.SCL, Raspberry_Pi.GPIO3
  N7: NEOPIXEL1.Din, Raspberry_Pi.GPIO10
  N8: Raspberry_Pi.GPIO16, Bn_ST_2.Pin_1, Bn_ST_2.Pin_2

notes:
  HiFiBerry:
  GPIO 2
  GPIO 3
  GPIO 18
  GPIO 19
  GPIO 20
  GPIO 21
  Neopixel:
  GPIO 10
  5V
  GND
  Rotary Encoder:
  CLK GPIO 13
  DT GPIO 6
  SW GPIO 5
  5V
  GND
  OLED:
  SCL GPIO 3
  SDA GPIO 2
  5V
  GND
  Button 1:
  GPIO 12
  GND
  Button 2:
  GPIO 16
  GND

custom parts:
  Neopixel Strip -- White (30/m): These NeoPixel strips have 30 digitally-addressable pixel LEDs per meter and are very affordable and are only 12.5 mm wide, 10 mm if you remove the strip from the casing.
